// Digital circuit part_c.dig as structural Verilog
module part_c (
  input  in_0,
  input  in_1,
  input  in_2,
  output out_1
);

  wire pfet_1_d, pfet_2_d, pfet_3_d;

  PFET pfet_1 (.G(in_0), .S(1'b1), .D(pfet_1_d));
  NFET nfet_1 (.G(in_0), .D(pfet_1_d), .S(1'b0));
  PFET pfet_2 (.G(in_1), .S(1'b1), .D(pfet_2_d));
  NFET nfet_2 (.G(in_1), .D(pfet_2_d), .S(1'b0));
  PFET pfet_3 (.G(in_2), .S(1'b1), .D(pfet_3_d));
  NFET nfet_3 (.G(in_2), .D(pfet_3_d), .S(1'b0));
  PFET pfet_4 ();  // open: G, S, D
  NFET nfet_4 ();  // open: G, D, S

  // Notes on the sheet:
  //   in_0 in_1 in_2 | out_0 
  //   0 0 0 | 1 
  //   0 0 1 | 0 
  //   0 1 0 | 0 
  //   0 1 1 | 0 
  //   1 0 0 | 0 
  //   1 0 1 | 0 
  //   1 1 0 | 1 
  //   1 1 1 | 1
  //   in0'*in1'*in2' + in0*in1
endmodule
