// Digital circuit lab2_part1.dig as structural Verilog
module lab2_part1 (
  input  inA_0,
  input  inA_1,
  input  inA_2,
  input  inA_3,
  input  inB_0,
  input  inB_1,
  input  inB_2,
  input  inB_3,
  input  op,
  output out0,
  output out1,
  output out2,
  output out3,
  output overflow
);

  Add add_1 ();  // open: a, b, c_i, s, c_o
  Sub sub_1 ();  // open: a, b, c_i, s, c_o
  Multiplexer #(.Bits(4), .Selector_Bits(3)) multiplexer_1 ();  // open: sel, in_0, in_1, in_2, in_3, in_4, in_5, in_6, in_7, out

  // Notes on the sheet:
  //   Interface (do not edit the content inside this box)
  //   Inputs
  //   Result of doing the addition (op=0) / subtraction (op=1) and overflow bit:
  //   Output number (in 2's complement)
  //   First Number (in 2's complement)
  //   Second number (in 2's complement)
endmodule

/* Test case grading:
inA_0 inA_1 inA_2 inA_3 inB_0 inB_1 inB_2 inB_3 op out0 out1 out2 out3 overflow 

 0 0 0 0 0 0 0 0 0 0 0 0 0 0
 0 0 0 0 0 0 0 0 1 0 0 0 0 0
 0 0 0 0 0 0 0 1 0 0 0 0 1 0
 0 0 0 0 0 0 0 1 1 0 0 0 1 1
 0 0 0 0 0 0 1 0 0 0 0 1 0 0
 0 0 0 0 0 0 1 0 1 0 0 1 1 0
 0 0 0 0 0 0 1 1 0 0 0 1 1 0
 0 0 0 0 0 0 1 1 1 0 0 1 0 0
 0 0 0 0 0 1 0 0 0 0 1 0 0 0
 0 0 0 0 0 1 0 0 1 0 1 1 1 0
 0 0 0 0 0 1 0 1 0 0 1 0 1 0
 0 0 0 0 0 1 0 1 1 0 1 1 0 0
 0 0 0 0 0 1 1 0 0 0 1 1 0 0
 0 0 0 0 0 1 1 0 1 0 1 0 1 0
 0 0 0 0 0 1 1 1 0 0 1 1 1 0
 0 0 0 0 0 1 1 1 1 0 1 0 0 0
 0 0 0 0 1 0 0 0 0 1 0 0 0 0
 0 0 0 0 1 0 0 0 1 1 1 1 1 0
 0 0 0 0 1 0 0 1 0 1 0 0 1 0
 0 0 0 0 1 0 0 1 1 1 1 1 0 0
 0 0 0 0 1 0 1 0 0 1 0 1 0 0
 0 0 0 0 1 0 1 0 1 1 1 0 1 0
 0 0 0 0 1 0 1 1 0 1 0 1 1 0
 0 0 0 0 1 0 1 1 1 1 1 0 0 0
 0 0 0 0 1 1 0 0 0 1 1 0 0 0
 0 0 0 0 1 1 0 0 1 1 0 1 1 0
 0 0 0 0 1 1 0 1 0 1 1 0 1 0
 0 0 0 0 1 1 0 1 1 1 0 1 0 0
 0 0 0 0 1 1 1 0 0 1 1 1 0 0
 0 0 0 0 1 1 1 0 1 1 0 0 1 0
 0 0 0 0 1 1 1 1 0 1 1 1 1 0
 0 0 0 0 1 1 1 1 1 1 0 0 0 0
 0 0 0 1 0 0 0 0 0 0 0 0 1 0
 0 0 0 1 0 0 0 0 1 0 0 0 1 0
 0 0 0 1 0 0 0 1 0 0 0 0 0 1
 0 0 0 1 0 0 0 1 1 0 0 0 0 0
 0 0 0 1 0 0 1 0 0 0 0 1 1 0
 0 0 0 1 0 0 1 0 1 0 0 1 0 1
 0 0 0 1 0 0 1 1 0 0 0 1 0 1
 0 0 0 1 0 0 1 1 1 0 0 1 1 0
 0 0 0 1 0 1 0 0 0 0 1 0 1 0
 0 0 0 1 0 1 0 0 1 0 1 1 0 1
 0 0 0 1 0 1 0 1 0 0 1 0 0 1
 0 0 0 1 0 1 0 1 1 0 1 1 1 0
 0 0 0 1 0 1 1 0 0 0 1 1 1 0
 0 0 0 1 0 1 1 0 1 0 1 0 0 1
 0 0 0 1 0 1 1 1 0 0 1 1 0 1
 0 0 0 1 0 1 1 1 1 0 1 0 1 0
 0 0 0 1 1 0 0 0 0 1 0 0 1 0
 0 0 0 1 1 0 0 0 1 1 1 1 0 1
 0 0 0 1 1 0 0 1 0 1 0 0 0 1
 0 0 0 1 1 0 0 1 1 1 1 1 1 0
 0 0 0 1 1 0 1 0 0 1 0 1 1 0
 0 0 0 1 1 0 1 0 1 1 1 0 0 1
 0 0 0 1 1 0 1 1 0 1 0 1 0 1
 0 0 0 1 1 0 1 1 1 1 1 0 1 0
 0 0 0 1 1 1 0 0 0 1 1 0 1 0
 0 0 0 1 1 1 0 0 1 1 0 1 0 1
 0 0 0 1 1 1 0 1 0 1 1 0 0 1
 0 0 0 1 1 1 0 1 1 1 0 1 1 0
 0 0 0 1 1 1 1 0 0 1 1 1 1 0
 0 0 0 1 1 1 1 0 1 1 0 0 0 1
 0 0 0 1 1 1 1 1 0 1 1 1 0 1
 0 0 0 1 1 1 1 1 1 1 0 0 1 0
 0 0 1 0 0 0 0 0 0 0 0 1 0 0
 0 0 1 0 0 0 0 0 1 0 0 1 0 0
 0 0 1 0 0 0 0 1 0 0 0 1 1 0
 0 0 1 0 0 0 0 1 1 0 0 1 1 1
 0 0 1 0 0 0 1 0 0 0 0 0 1 1
 0 0 1 0 0 0 1 0 1 0 0 0 0 0
 0 0 1 0 0 0 1 1 0 0 0 0 0 0
 0 0 1 0 0 0 1 1 1 0 0 0 1 1
 0 0 1 0 0 1 0 0 0 0 1 1 0 0
 0 0 1 0 0 1 0 0 1 0 1 0 0 0
 0 0 1 0 0 1 0 1 0 0 1 1 1 0
 0 0 1 0 0 1 0 1 1 0 1 0 1 1
 0 0 1 0 0 1 1 0 0 0 1 0 1 1
 0 0 1 0 0 1 1 0 1 0 1 1 1 0
 0 0 1 0 0 1 1 1 0 0 1 0 0 0
 0 0 1 0 0 1 1 1 1 0 1 1 0 0
 0 0 1 0 1 0 0 0 0 1 0 1 0 0
 0 0 1 0 1 0 0 0 1 1 1 0 0 0
 0 0 1 0 1 0 0 1 0 1 0 1 1 0
 0 0 1 0 1 0 0 1 1 1 1 0 1 1
 0 0 1 0 1 0 1 0 0 1 0 0 1 1
 0 0 1 0 1 0 1 0 1 1 1 1 1 0
 0 0 1 0 1 0 1 1 0 1 0 0 0 0
 0 0 1 0 1 0 1 1 1 1 1 1 0 0
 0 0 1 0 1 1 0 0 0 1 1 1 0 0
 0 0 1 0 1 1 0 0 1 1 0 0 0 0
 0 0 1 0 1 1 0 1 0 1 1 1 1 0
 0 0 1 0 1 1 0 1 1 1 0 0 1 1
 0 0 1 0 1 1 1 0 0 1 1 0 1 1
 0 0 1 0 1 1 1 0 1 1 0 1 1 0
 0 0 1 0 1 1 1 1 0 1 1 0 0 0
 0 0 1 0 1 1 1 1 1 1 0 1 0 0
 0 0 1 1 0 0 0 0 0 0 0 1 1 0
 0 0 1 1 0 0 0 0 1 0 0 1 1 0
 0 0 1 1 0 0 0 1 0 0 0 1 0 1
 0 0 1 1 0 0 0 1 1 0 0 1 0 0
 0 0 1 1 0 0 1 0 0 0 0 0 0 0
 0 0 1 1 0 0 1 0 1 0 0 0 1 0
 0 0 1 1 0 0 1 1 0 0 0 0 1 0
 0 0 1 1 0 0 1 1 1 0 0 0 0 0
 0 0 1 1 0 1 0 0 0 0 1 1 1 0
 0 0 1 1 0 1 0 0 1 0 1 0 1 0
 0 0 1 1 0 1 0 1 0 0 1 1 0 1
 0 0 1 1 0 1 0 1 1 0 1 0 0 0
 0 0 1 1 0 1 1 0 0 0 1 0 0 0
 0 0 1 1 0 1 1 0 1 0 1 1 0 1
 0 0 1 1 0 1 1 1 0 0 1 0 1 0
 0 0 1 1 0 1 1 1 1 0 1 1 1 0
 0 0 1 1 1 0 0 0 0 1 0 1 1 0
 0 0 1 1 1 0 0 0 1 1 1 0 1 0
 0 0 1 1 1 0 0 1 0 1 0 1 0 1
 0 0 1 1 1 0 0 1 1 1 1 0 0 0
 0 0 1 1 1 0 1 0 0 1 0 0 0 0
 0 0 1 1 1 0 1 0 1 1 1 1 0 1
 0 0 1 1 1 0 1 1 0 1 0 0 1 0
 0 0 1 1 1 0 1 1 1 1 1 1 1 0
 0 0 1 1 1 1 0 0 0 1 1 1 1 0
 0 0 1 1 1 1 0 0 1 1 0 0 1 0
 0 0 1 1 1 1 0 1 0 1 1 1 0 1
 0 0 1 1 1 1 0 1 1 1 0 0 0 0
 0 0 1 1 1 1 1 0 0 1 1 0 0 0
 0 0 1 1 1 1 1 0 1 1 0 1 0 1
 0 0 1 1 1 1 1 1 0 1 1 0 1 0
 0 0 1 1 1 1 1 1 1 1 0 1 1 0
 0 1 0 0 0 0 0 0 0 0 1 0 0 0
 0 1 0 0 0 0 0 0 1 0 1 0 0 0
 0 1 0 0 0 0 0 1 0 0 1 0 1 0
 0 1 0 0 0 0 0 1 1 0 1 0 1 1
 0 1 0 0 0 0 1 0 0 0 1 1 0 0
 0 1 0 0 0 0 1 0 1 0 1 1 1 0
 0 1 0 0 0 0 1 1 0 0 1 1 1 0
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*/
